// Digital circuit Hypertron 32-bit ALU v1.1.dig as structural Verilog
module Hypertron_32_bit_ALU_v1_1 (
  input  [4:0] OPCODE,
  input  [31:0] A,
  input  [31:0] B,
  input  clock,
  output [31:0] Out,
  output [31:0] Over
);

  wire add_1_c_o, bitselector_1_out, comparator_1_eq, comparator_1_gt, comparator_1_lt, comparator_2_eq,
       comparator_2_gt, comparator_2_lt, comparator_3_eq, comparator_3_gt, comparator_3_lt, sub_1_c_o;
  wire [5:0] bitcount_1_out;
  wire [31:0] _1a, _1b, _2a, _2b, _3a, _3b, _4a, _4b, _5a, _5b, _6a, _6b, _7a, _8a, _8b, _9a, _9b, _10a,
       _10b, _11a, _11b, _12a, _12b, _13a, _13b, _14a, _15a, _16a, _16b, _17a, _17b, _18a, _18b, _19a, _19b,
       _20a, _20b, _21a, demultiplexer_1_out_6, demultiplexer_1_out_13, demultiplexer_1_out_14,
       demultiplexer_1_out_20, demultiplexer_1_out_21, demultiplexer_1_out_22, demultiplexer_1_out_23,
       demultiplexer_1_out_24, demultiplexer_1_out_25, demultiplexer_1_out_26, demultiplexer_1_out_27,
       demultiplexer_1_out_28, demultiplexer_1_out_29, demultiplexer_1_out_30, demultiplexer_1_out_31,
       demultiplexer_2_out_21, demultiplexer_2_out_22, demultiplexer_2_out_23, demultiplexer_2_out_24,
       demultiplexer_2_out_25, demultiplexer_2_out_26, demultiplexer_2_out_27, demultiplexer_2_out_28,
       demultiplexer_2_out_29, demultiplexer_2_out_30, demultiplexer_2_out_31, Out1, Out2, Out3, Out4, Out5,
       Out6, Out7, Out8, Out9, Out10, Out11, Out12, Out13, Out14, Out15, Out16, Out17, Out18, Out20, Out21,
       R1, R2, R3, R4;
  wire [63:0] bitextender_1_out;

  Demultiplexer #(.Selector_Bits(5), .Bits(32)) demultiplexer_1 (
    .sel(OPCODE), .in(B), .out_0(_1b), .out_1(_2b), .out_2(_3b), .out_3(_4b), .out_4(_5b), .out_5(_6b),
    .out_6(demultiplexer_1_out_6), .out_7(_8b), .out_8(_9b), .out_9(_10b), .out_10(_11b), .out_11(_12b),
    .out_12(_13b), .out_13(demultiplexer_1_out_13), .out_14(demultiplexer_1_out_14), .out_15(_16b),
    .out_16(_17b), .out_17(_18b), .out_18(_19b), .out_19(_20b), .out_20(demultiplexer_1_out_20),
    .out_21(demultiplexer_1_out_21), .out_22(demultiplexer_1_out_22), .out_23(demultiplexer_1_out_23),
    .out_24(demultiplexer_1_out_24), .out_25(demultiplexer_1_out_25), .out_26(demultiplexer_1_out_26),
    .out_27(demultiplexer_1_out_27), .out_28(demultiplexer_1_out_28), .out_29(demultiplexer_1_out_29),
    .out_30(demultiplexer_1_out_30), .out_31(demultiplexer_1_out_31));
  BitExtender #(.inputBits(32), .outputBits(64)) bitextender_1 (.in(_16a), .out(bitextender_1_out));
  Demultiplexer #(.Selector_Bits(5), .Bits(32)) demultiplexer_2 (
    .sel(OPCODE), .in(A), .out_0(_1a), .out_1(_2a), .out_2(_3a), .out_3(_4a), .out_4(_5a), .out_5(_6a),
    .out_6(_7a), .out_7(_8a), .out_8(_9a), .out_9(_10a), .out_10(_11a), .out_11(_12a), .out_12(_13a),
    .out_13(_14a), .out_14(_15a), .out_15(_16a), .out_16(_17a), .out_17(_18a), .out_18(_19a), .out_19(_20a),
    .out_20(_21a), .out_21(demultiplexer_2_out_21), .out_22(demultiplexer_2_out_22),
    .out_23(demultiplexer_2_out_23), .out_24(demultiplexer_2_out_24), .out_25(demultiplexer_2_out_25),
    .out_26(demultiplexer_2_out_26), .out_27(demultiplexer_2_out_27), .out_28(demultiplexer_2_out_28),
    .out_29(demultiplexer_2_out_29), .out_30(demultiplexer_2_out_30), .out_31(demultiplexer_2_out_31));
  assign Out1 = _1a & _1b;  // And and_1, 32 bits wide
  assign Out2 = ~(_2a & _2b);  // NAnd nand_1, 32 bits wide
  assign Out3 = _3a | _3b;  // Or or_1, 32 bits wide
  assign Out4 = ~(_4a | _4b);  // NOr nor_1, 32 bits wide
  assign Out5 = _5a ^ _5b;  // XOr xor_1, 32 bits wide
  assign Out6 = ~(_6a ^ _6b);  // XNOr xnor_1, 32 bits wide
  assign Out7 = ~_7a;  // Not not_1, 32 bits wide
  Add #(.Bits(32)) add_1 (.a(_8a), .b(_8b), .c_i(1'b0), .s(Out8), .c_o(add_1_c_o));
  Sub #(.Bits(32)) sub_1 (.a(_9a), .b(_9b), .c_i(1'b0), .s(Out9), .c_o(sub_1_c_o));
  Mul #(.Bits(32)) mul_1 (.a(_10a), .b(_10b), .mul({R3, Out10}));
  Div #(.Bits(32)) div_1 (.a(_11a), .b(_11b), .q(Out11), .r(R4));
  BarrelShifter #(.Bits(32), .barrelShifterMode("arithmetic")) barrelshifter_1 (
    .in(_12a), .shift(_12b[5:0]), .out(Out12));
  Comparator #(.Bits(32)) comparator_1 (
    .a(_13a), .b(_13b), .gt(comparator_1_gt), .eq(comparator_1_eq), .lt(comparator_1_lt));
  Neg #(.Bits(32)) neg_1 (.in(_14a), .out(Out14));
  BitCount #(.Bits(32)) bitcount_1 (.in(_15a), .out(bitcount_1_out));
  BitSelector #(.Selector_Bits(6)) bitselector_1 (.in(bitextender_1_out), .sel(_16b[5:0]), .out(bitselector_1_out));
  Comparator #(.Bits(32)) comparator_2 (
    .a(_17a), .b(_17b), .gt(comparator_2_gt), .eq(comparator_2_eq), .lt(comparator_2_lt));
  Comparator #(.Bits(32)) comparator_3 (
    .a(_18a), .b(_18b), .gt(comparator_3_gt), .eq(comparator_3_eq), .lt(comparator_3_lt));
  BarrelShifter #(.Bits(32), .barrelShifterMode("arithmetic"), .direction("right")) barrelshifter_2 (
    .in(_20a), .shift(_20b[5:0]), .out(Out20));
  PRNG #(.Bits(32)) prng_1 (.S(_21a), .se(1'b1), .ne(1'b0), .C(clock), .R(Out21));
  BitExtender #(.inputBits(1), .outputBits(32)) bitextender_2 (.in(add_1_c_o), .out(R1));
  BitExtender #(.inputBits(1), .outputBits(32)) bitextender_3 (.in(sub_1_c_o), .out(R2));
  BitExtender #(.inputBits(1), .outputBits(32)) bitextender_4 (.in(comparator_1_eq), .out(Out13));
  BitExtender #(.inputBits(6), .outputBits(32)) bitextender_5 (.in(bitcount_1_out), .out(Out15));
  BitExtender #(.inputBits(1), .outputBits(32)) bitextender_6 (.in(bitselector_1_out), .out(Out16));
  BitExtender #(.inputBits(1), .outputBits(32)) bitextender_7 (.in(comparator_2_gt), .out(Out17));
  BitExtender #(.inputBits(1), .outputBits(32)) bitextender_8 (.in(comparator_3_lt), .out(Out18));
  Multiplexer #(.Selector_Bits(5), .Bits(32)) multiplexer_1 (
    .sel(OPCODE), .in_0({32{1'b0}}), .in_1({32{1'b0}}), .in_2({32{1'b0}}), .in_3({32{1'b0}}),
    .in_4({32{1'b0}}), .in_5({32{1'b0}}), .in_6({32{1'b0}}), .in_7(R1), .in_8(R2), .in_9(R3), .in_10(R4),
    .in_11({32{1'b0}}), .in_12({32{1'b0}}), .in_13({32{1'b0}}), .in_14({32{1'b0}}), .in_15({32{1'b0}}),
    .in_16({32{1'b0}}), .in_17({32{1'b0}}), .in_18({32{1'b0}}), .in_19({32{1'b0}}), .in_20({32{1'b0}}),
    .in_21({32{1'b0}}), .in_22({32{1'b0}}), .in_23({32{1'b0}}), .in_24({32{1'b0}}), .in_25({32{1'b0}}),
    .in_26({32{1'b0}}), .in_27({32{1'b0}}), .in_28({32{1'b0}}), .in_29({32{1'b0}}), .in_30({32{1'b0}}),
    .in_31({32{1'b0}}), .out(Over));
  Multiplexer #(.Selector_Bits(5), .Bits(32)) multiplexer_2 (
    .sel(OPCODE), .in_0(Out1), .in_1(Out2), .in_2(Out3), .in_3(Out4), .in_4(Out5), .in_5(Out6), .in_6(Out7),
    .in_7(Out8), .in_8(Out9), .in_9(Out10), .in_10(Out11), .in_11(Out12), .in_12(Out13), .in_13(Out14),
    .in_14(Out15), .in_15(Out16), .in_16(Out17), .in_17(Out18), .in_18({32{1'b0}}), .in_19(Out20),
    .in_20(Out21), .in_21({32{1'b0}}), .in_22({32{1'b0}}), .in_23({32{1'b0}}), .in_24({32{1'b0}}),
    .in_25({32{1'b0}}), .in_26({32{1'b0}}), .in_27({32{1'b0}}), .in_28({32{1'b0}}), .in_29({32{1'b0}}),
    .in_30({32{1'b0}}), .in_31({32{1'b0}}), .out(Out));
  // also tied to GND on the sheet: {demultiplexer_1_out_6[0], demultiplexer_1_out_6[1], demultiplexer_1_out_6[2], demultiplexer_1_out_6[3], demultiplexer_1_out_6[4], demultiplexer_1_out_6[5], demultiplexer_1_out_6[6], demultiplexer_1_out_6[7], demultiplexer_1_out_6[8], demultiplexer_1_out_6[9], demultiplexer_1_out_6[10], demultiplexer_1_out_6[11], demultiplexer_1_out_6[12], demultiplexer_1_out_6[13], demultiplexer_1_out_6[14], demultiplexer_1_out_6[15], demultiplexer_1_out_6[16], demultiplexer_1_out_6[17], demultiplexer_1_out_6[18], demultiplexer_1_out_6[19], demultiplexer_1_out_6[20], demultiplexer_1_out_6[21], demultiplexer_1_out_6[22], demultiplexer_1_out_6[23], demultiplexer_1_out_6[24], demultiplexer_1_out_6[25], demultiplexer_1_out_6[26], demultiplexer_1_out_6[27], demultiplexer_1_out_6[28], demultiplexer_1_out_6[29], demultiplexer_1_out_6[30], demultiplexer_1_out_6[31], demultiplexer_1_out_13[0], demultiplexer_1_out_13[1], demultiplexer_1_out_13[2], demultiplexer_1_out_13[3], demultiplexer_1_out_13[4], demultiplexer_1_out_13[5], demultiplexer_1_out_13[6], demultiplexer_1_out_13[7], demultiplexer_1_out_13[8], demultiplexer_1_out_13[9], demultiplexer_1_out_13[10], demultiplexer_1_out_13[11], demultiplexer_1_out_13[12], demultiplexer_1_out_13[13], demultiplexer_1_out_13[14], demultiplexer_1_out_13[15], demultiplexer_1_out_13[16], demultiplexer_1_out_13[17], demultiplexer_1_out_13[18], demultiplexer_1_out_13[19], demultiplexer_1_out_13[20], demultiplexer_1_out_13[21], demultiplexer_1_out_13[22], demultiplexer_1_out_13[23], demultiplexer_1_out_13[24], demultiplexer_1_out_13[25], demultiplexer_1_out_13[26], demultiplexer_1_out_13[27], demultiplexer_1_out_13[28], demultiplexer_1_out_13[29], demultiplexer_1_out_13[30], demultiplexer_1_out_13[31], demultiplexer_1_out_14[0], demultiplexer_1_out_14[1], demultiplexer_1_out_14[2], demultiplexer_1_out_14[3], demultiplexer_1_out_14[4], demultiplexer_1_out_14[5], demultiplexer_1_out_14[6], demultiplexer_1_out_14[7], demultiplexer_1_out_14[8], demultiplexer_1_out_14[9], demultiplexer_1_out_14[10], demultiplexer_1_out_14[11], demultiplexer_1_out_14[12], demultiplexer_1_out_14[13], demultiplexer_1_out_14[14], demultiplexer_1_out_14[15], demultiplexer_1_out_14[16], demultiplexer_1_out_14[17], demultiplexer_1_out_14[18], demultiplexer_1_out_14[19], demultiplexer_1_out_14[20], demultiplexer_1_out_14[21], demultiplexer_1_out_14[22], demultiplexer_1_out_14[23], demultiplexer_1_out_14[24], demultiplexer_1_out_14[25], demultiplexer_1_out_14[26], demultiplexer_1_out_14[27], demultiplexer_1_out_14[28], demultiplexer_1_out_14[29], demultiplexer_1_out_14[30], demultiplexer_1_out_14[31], demultiplexer_1_out_20[0], demultiplexer_1_out_20[1], demultiplexer_1_out_20[2], demultiplexer_1_out_20[3], demultiplexer_1_out_20[4], demultiplexer_1_out_20[5], demultiplexer_1_out_20[6], demultiplexer_1_out_20[7], demultiplexer_1_out_20[8], demultiplexer_1_out_20[9], demultiplexer_1_out_20[10], demultiplexer_1_out_20[11], demultiplexer_1_out_20[12], demultiplexer_1_out_20[13], demultiplexer_1_out_20[14], demultiplexer_1_out_20[15], demultiplexer_1_out_20[16], demultiplexer_1_out_20[17], demultiplexer_1_out_20[18], demultiplexer_1_out_20[19], demultiplexer_1_out_20[20], demultiplexer_1_out_20[21], demultiplexer_1_out_20[22], demultiplexer_1_out_20[23], demultiplexer_1_out_20[24], demultiplexer_1_out_20[25], demultiplexer_1_out_20[26], demultiplexer_1_out_20[27], demultiplexer_1_out_20[28], demultiplexer_1_out_20[29], demultiplexer_1_out_20[30], demultiplexer_1_out_20[31], demultiplexer_1_out_21[0], demultiplexer_1_out_21[1], demultiplexer_1_out_21[2], demultiplexer_1_out_21[3], demultiplexer_1_out_21[4], demultiplexer_1_out_21[5], demultiplexer_1_out_21[6], demultiplexer_1_out_21[7], demultiplexer_1_out_21[8], demultiplexer_1_out_21[9], demultiplexer_1_out_21[10], demultiplexer_1_out_21[11], demultiplexer_1_out_21[12], demultiplexer_1_out_21[13], demultiplexer_1_out_21[14], demultiplexer_1_out_21[15], demultiplexer_1_out_21[16], demultiplexer_1_out_21[17], demultiplexer_1_out_21[18], demultiplexer_1_out_21[19], demultiplexer_1_out_21[20], demultiplexer_1_out_21[21], demultiplexer_1_out_21[22], demultiplexer_1_out_21[23], demultiplexer_1_out_21[24], demultiplexer_1_out_21[25], demultiplexer_1_out_21[26], demultiplexer_1_out_21[27], demultiplexer_1_out_21[28], demultiplexer_1_out_21[29], demultiplexer_1_out_21[30], demultiplexer_1_out_21[31], demultiplexer_1_out_22[0], demultiplexer_1_out_22[1], demultiplexer_1_out_22[2], demultiplexer_1_out_22[3], demultiplexer_1_out_22[4], demultiplexer_1_out_22[5], demultiplexer_1_out_22[6], demultiplexer_1_out_22[7], demultiplexer_1_out_22[8], demultiplexer_1_out_22[9], demultiplexer_1_out_22[10], demultiplexer_1_out_22[11], demultiplexer_1_out_22[12], demultiplexer_1_out_22[13], demultiplexer_1_out_22[14], demultiplexer_1_out_22[15], demultiplexer_1_out_22[16], demultiplexer_1_out_22[17], demultiplexer_1_out_22[18], demultiplexer_1_out_22[19], demultiplexer_1_out_22[20], demultiplexer_1_out_22[21], demultiplexer_1_out_22[22], demultiplexer_1_out_22[23], demultiplexer_1_out_22[24], demultiplexer_1_out_22[25], demultiplexer_1_out_22[26], demultiplexer_1_out_22[27], demultiplexer_1_out_22[28], demultiplexer_1_out_22[29], demultiplexer_1_out_22[30], demultiplexer_1_out_22[31], demultiplexer_1_out_23[0], demultiplexer_1_out_23[1], demultiplexer_1_out_23[2], demultiplexer_1_out_23[3], demultiplexer_1_out_23[4], demultiplexer_1_out_23[5], demultiplexer_1_out_23[6], demultiplexer_1_out_23[7], demultiplexer_1_out_23[8], demultiplexer_1_out_23[9], demultiplexer_1_out_23[10], demultiplexer_1_out_23[11], demultiplexer_1_out_23[12], demultiplexer_1_out_23[13], demultiplexer_1_out_23[14], demultiplexer_1_out_23[15], demultiplexer_1_out_23[16], demultiplexer_1_out_23[17], demultiplexer_1_out_23[18], demultiplexer_1_out_23[19], demultiplexer_1_out_23[20], demultiplexer_1_out_23[21], demultiplexer_1_out_23[22], demultiplexer_1_out_23[23], demultiplexer_1_out_23[24], demultiplexer_1_out_23[25], demultiplexer_1_out_23[26], demultiplexer_1_out_23[27], demultiplexer_1_out_23[28], demultiplexer_1_out_23[29], demultiplexer_1_out_23[30], demultiplexer_1_out_23[31], demultiplexer_1_out_24[0], demultiplexer_1_out_24[1], demultiplexer_1_out_24[2], demultiplexer_1_out_24[3], demultiplexer_1_out_24[4], demultiplexer_1_out_24[5], demultiplexer_1_out_24[6], demultiplexer_1_out_24[7], demultiplexer_1_out_24[8], demultiplexer_1_out_24[9], demultiplexer_1_out_24[10], demultiplexer_1_out_24[11], demultiplexer_1_out_24[12], demultiplexer_1_out_24[13], demultiplexer_1_out_24[14], demultiplexer_1_out_24[15], demultiplexer_1_out_24[16], demultiplexer_1_out_24[17], demultiplexer_1_out_24[18], demultiplexer_1_out_24[19], demultiplexer_1_out_24[20], demultiplexer_1_out_24[21], demultiplexer_1_out_24[22], demultiplexer_1_out_24[23], demultiplexer_1_out_24[24], demultiplexer_1_out_24[25], demultiplexer_1_out_24[26], demultiplexer_1_out_24[27], demultiplexer_1_out_24[28], demultiplexer_1_out_24[29], demultiplexer_1_out_24[30], demultiplexer_1_out_24[31], demultiplexer_1_out_25[0], demultiplexer_1_out_25[1], demultiplexer_1_out_25[2], demultiplexer_1_out_25[3], demultiplexer_1_out_25[4], demultiplexer_1_out_25[5], demultiplexer_1_out_25[6], demultiplexer_1_out_25[7], demultiplexer_1_out_25[8], demultiplexer_1_out_25[9], demultiplexer_1_out_25[10], demultiplexer_1_out_25[11], demultiplexer_1_out_25[12], demultiplexer_1_out_25[13], demultiplexer_1_out_25[14], demultiplexer_1_out_25[15], demultiplexer_1_out_25[16], demultiplexer_1_out_25[17], demultiplexer_1_out_25[18], demultiplexer_1_out_25[19], demultiplexer_1_out_25[20], demultiplexer_1_out_25[21], demultiplexer_1_out_25[22], demultiplexer_1_out_25[23], demultiplexer_1_out_25[24], demultiplexer_1_out_25[25], demultiplexer_1_out_25[26], demultiplexer_1_out_25[27], demultiplexer_1_out_25[28], demultiplexer_1_out_25[29], demultiplexer_1_out_25[30], demultiplexer_1_out_25[31], demultiplexer_1_out_26[0], demultiplexer_1_out_26[1], demultiplexer_1_out_26[2], demultiplexer_1_out_26[3], demultiplexer_1_out_26[4], demultiplexer_1_out_26[5], demultiplexer_1_out_26[6], demultiplexer_1_out_26[7], demultiplexer_1_out_26[8], demultiplexer_1_out_26[9], demultiplexer_1_out_26[10], demultiplexer_1_out_26[11], demultiplexer_1_out_26[12], demultiplexer_1_out_26[13], demultiplexer_1_out_26[14], demultiplexer_1_out_26[15], demultiplexer_1_out_26[16], demultiplexer_1_out_26[17], demultiplexer_1_out_26[18], demultiplexer_1_out_26[19], demultiplexer_1_out_26[20], demultiplexer_1_out_26[21], demultiplexer_1_out_26[22], demultiplexer_1_out_26[23], demultiplexer_1_out_26[24], demultiplexer_1_out_26[25], demultiplexer_1_out_26[26], demultiplexer_1_out_26[27], demultiplexer_1_out_26[28], demultiplexer_1_out_26[29], demultiplexer_1_out_26[30], demultiplexer_1_out_26[31], demultiplexer_1_out_27[0], demultiplexer_1_out_27[1], demultiplexer_1_out_27[2], demultiplexer_1_out_27[3], demultiplexer_1_out_27[4], demultiplexer_1_out_27[5], demultiplexer_1_out_27[6], demultiplexer_1_out_27[7], demultiplexer_1_out_27[8], demultiplexer_1_out_27[9], demultiplexer_1_out_27[10], demultiplexer_1_out_27[11], demultiplexer_1_out_27[12], demultiplexer_1_out_27[13], demultiplexer_1_out_27[14], demultiplexer_1_out_27[15], demultiplexer_1_out_27[16], demultiplexer_1_out_27[17], demultiplexer_1_out_27[18], demultiplexer_1_out_27[19], demultiplexer_1_out_27[20], demultiplexer_1_out_27[21], demultiplexer_1_out_27[22], demultiplexer_1_out_27[23], demultiplexer_1_out_27[24], demultiplexer_1_out_27[25], demultiplexer_1_out_27[26], demultiplexer_1_out_27[27], demultiplexer_1_out_27[28], demultiplexer_1_out_27[29], demultiplexer_1_out_27[30], demultiplexer_1_out_27[31], demultiplexer_1_out_28[0], demultiplexer_1_out_28[1], demultiplexer_1_out_28[2], demultiplexer_1_out_28[3], demultiplexer_1_out_28[4], demultiplexer_1_out_28[5], demultiplexer_1_out_28[6], demultiplexer_1_out_28[7], demultiplexer_1_out_28[8], demultiplexer_1_out_28[9], demultiplexer_1_out_28[10], demultiplexer_1_out_28[11], demultiplexer_1_out_28[12], demultiplexer_1_out_28[13], demultiplexer_1_out_28[14], demultiplexer_1_out_28[15], demultiplexer_1_out_28[16], demultiplexer_1_out_28[17], demultiplexer_1_out_28[18], demultiplexer_1_out_28[19], demultiplexer_1_out_28[20], demultiplexer_1_out_28[21], demultiplexer_1_out_28[22], demultiplexer_1_out_28[23], demultiplexer_1_out_28[24], demultiplexer_1_out_28[25], demultiplexer_1_out_28[26], demultiplexer_1_out_28[27], demultiplexer_1_out_28[28], demultiplexer_1_out_28[29], demultiplexer_1_out_28[30], demultiplexer_1_out_28[31], demultiplexer_1_out_29[0], demultiplexer_1_out_29[1], demultiplexer_1_out_29[2], demultiplexer_1_out_29[3], demultiplexer_1_out_29[4], demultiplexer_1_out_29[5], demultiplexer_1_out_29[6], demultiplexer_1_out_29[7], demultiplexer_1_out_29[8], demultiplexer_1_out_29[9], demultiplexer_1_out_29[10], demultiplexer_1_out_29[11], demultiplexer_1_out_29[12], demultiplexer_1_out_29[13], demultiplexer_1_out_29[14], demultiplexer_1_out_29[15], demultiplexer_1_out_29[16], demultiplexer_1_out_29[17], demultiplexer_1_out_29[18], demultiplexer_1_out_29[19], demultiplexer_1_out_29[20], demultiplexer_1_out_29[21], demultiplexer_1_out_29[22], demultiplexer_1_out_29[23], demultiplexer_1_out_29[24], demultiplexer_1_out_29[25], demultiplexer_1_out_29[26], demultiplexer_1_out_29[27], demultiplexer_1_out_29[28], demultiplexer_1_out_29[29], demultiplexer_1_out_29[30], demultiplexer_1_out_29[31], demultiplexer_1_out_30[0], demultiplexer_1_out_30[1], demultiplexer_1_out_30[2], demultiplexer_1_out_30[3], demultiplexer_1_out_30[4], demultiplexer_1_out_30[5], demultiplexer_1_out_30[6], demultiplexer_1_out_30[7], demultiplexer_1_out_30[8], demultiplexer_1_out_30[9], demultiplexer_1_out_30[10], demultiplexer_1_out_30[11], demultiplexer_1_out_30[12], demultiplexer_1_out_30[13], demultiplexer_1_out_30[14], demultiplexer_1_out_30[15], demultiplexer_1_out_30[16], demultiplexer_1_out_30[17], demultiplexer_1_out_30[18], demultiplexer_1_out_30[19], demultiplexer_1_out_30[20], demultiplexer_1_out_30[21], demultiplexer_1_out_30[22], demultiplexer_1_out_30[23], demultiplexer_1_out_30[24], demultiplexer_1_out_30[25], demultiplexer_1_out_30[26], demultiplexer_1_out_30[27], demultiplexer_1_out_30[28], demultiplexer_1_out_30[29], demultiplexer_1_out_30[30], demultiplexer_1_out_30[31], demultiplexer_1_out_31[0], demultiplexer_1_out_31[1], demultiplexer_1_out_31[2], demultiplexer_1_out_31[3], demultiplexer_1_out_31[4], demultiplexer_1_out_31[5], demultiplexer_1_out_31[6], demultiplexer_1_out_31[7], demultiplexer_1_out_31[8], demultiplexer_1_out_31[9], demultiplexer_1_out_31[10], demultiplexer_1_out_31[11], demultiplexer_1_out_31[12], demultiplexer_1_out_31[13], demultiplexer_1_out_31[14], demultiplexer_1_out_31[15], demultiplexer_1_out_31[16], demultiplexer_1_out_31[17], demultiplexer_1_out_31[18], demultiplexer_1_out_31[19], demultiplexer_1_out_31[20], demultiplexer_1_out_31[21], demultiplexer_1_out_31[22], demultiplexer_1_out_31[23], demultiplexer_1_out_31[24], demultiplexer_1_out_31[25], demultiplexer_1_out_31[26], demultiplexer_1_out_31[27], demultiplexer_1_out_31[28], demultiplexer_1_out_31[29], demultiplexer_1_out_31[30], demultiplexer_1_out_31[31], demultiplexer_2_out_31[0], demultiplexer_2_out_31[1], demultiplexer_2_out_31[2], demultiplexer_2_out_31[3], demultiplexer_2_out_31[4], demultiplexer_2_out_31[5], demultiplexer_2_out_31[6], demultiplexer_2_out_31[7], demultiplexer_2_out_31[8], demultiplexer_2_out_31[9], demultiplexer_2_out_31[10], demultiplexer_2_out_31[11], demultiplexer_2_out_31[12], demultiplexer_2_out_31[13], demultiplexer_2_out_31[14], demultiplexer_2_out_31[15], demultiplexer_2_out_31[16], demultiplexer_2_out_31[17], demultiplexer_2_out_31[18], demultiplexer_2_out_31[19], demultiplexer_2_out_31[20], demultiplexer_2_out_31[21], demultiplexer_2_out_31[22], demultiplexer_2_out_31[23], demultiplexer_2_out_31[24], demultiplexer_2_out_31[25], demultiplexer_2_out_31[26], demultiplexer_2_out_31[27], demultiplexer_2_out_31[28], demultiplexer_2_out_31[29], demultiplexer_2_out_31[30], demultiplexer_2_out_31[31], demultiplexer_2_out_30[0], demultiplexer_2_out_30[1], demultiplexer_2_out_30[2], demultiplexer_2_out_30[3], demultiplexer_2_out_30[4], demultiplexer_2_out_30[5], demultiplexer_2_out_30[6], demultiplexer_2_out_30[7], demultiplexer_2_out_30[8], demultiplexer_2_out_30[9], demultiplexer_2_out_30[10], demultiplexer_2_out_30[11], demultiplexer_2_out_30[12], demultiplexer_2_out_30[13], demultiplexer_2_out_30[14], demultiplexer_2_out_30[15], demultiplexer_2_out_30[16], demultiplexer_2_out_30[17], demultiplexer_2_out_30[18], demultiplexer_2_out_30[19], demultiplexer_2_out_30[20], demultiplexer_2_out_30[21], demultiplexer_2_out_30[22], demultiplexer_2_out_30[23], demultiplexer_2_out_30[24], demultiplexer_2_out_30[25], demultiplexer_2_out_30[26], demultiplexer_2_out_30[27], demultiplexer_2_out_30[28], demultiplexer_2_out_30[29], demultiplexer_2_out_30[30], demultiplexer_2_out_30[31], demultiplexer_2_out_29[0], demultiplexer_2_out_29[1], demultiplexer_2_out_29[2], demultiplexer_2_out_29[3], demultiplexer_2_out_29[4], demultiplexer_2_out_29[5], demultiplexer_2_out_29[6], demultiplexer_2_out_29[7], demultiplexer_2_out_29[8], demultiplexer_2_out_29[9], demultiplexer_2_out_29[10], demultiplexer_2_out_29[11], demultiplexer_2_out_29[12], demultiplexer_2_out_29[13], demultiplexer_2_out_29[14], demultiplexer_2_out_29[15], demultiplexer_2_out_29[16], demultiplexer_2_out_29[17], demultiplexer_2_out_29[18], demultiplexer_2_out_29[19], demultiplexer_2_out_29[20], demultiplexer_2_out_29[21], demultiplexer_2_out_29[22], demultiplexer_2_out_29[23], demultiplexer_2_out_29[24], demultiplexer_2_out_29[25], demultiplexer_2_out_29[26], demultiplexer_2_out_29[27], demultiplexer_2_out_29[28], demultiplexer_2_out_29[29], demultiplexer_2_out_29[30], demultiplexer_2_out_29[31], demultiplexer_2_out_28[0], demultiplexer_2_out_28[1], demultiplexer_2_out_28[2], demultiplexer_2_out_28[3], demultiplexer_2_out_28[4], demultiplexer_2_out_28[5], demultiplexer_2_out_28[6], demultiplexer_2_out_28[7], demultiplexer_2_out_28[8], demultiplexer_2_out_28[9], demultiplexer_2_out_28[10], demultiplexer_2_out_28[11], demultiplexer_2_out_28[12], demultiplexer_2_out_28[13], demultiplexer_2_out_28[14], demultiplexer_2_out_28[15], demultiplexer_2_out_28[16], demultiplexer_2_out_28[17], demultiplexer_2_out_28[18], demultiplexer_2_out_28[19], demultiplexer_2_out_28[20], demultiplexer_2_out_28[21], demultiplexer_2_out_28[22], demultiplexer_2_out_28[23], demultiplexer_2_out_28[24], demultiplexer_2_out_28[25], demultiplexer_2_out_28[26], demultiplexer_2_out_28[27], demultiplexer_2_out_28[28], demultiplexer_2_out_28[29], demultiplexer_2_out_28[30], demultiplexer_2_out_28[31], demultiplexer_2_out_27[0], demultiplexer_2_out_27[1], demultiplexer_2_out_27[2], demultiplexer_2_out_27[3], demultiplexer_2_out_27[4], demultiplexer_2_out_27[5], demultiplexer_2_out_27[6], demultiplexer_2_out_27[7], demultiplexer_2_out_27[8], demultiplexer_2_out_27[9], demultiplexer_2_out_27[10], demultiplexer_2_out_27[11], demultiplexer_2_out_27[12], demultiplexer_2_out_27[13], demultiplexer_2_out_27[14], demultiplexer_2_out_27[15], demultiplexer_2_out_27[16], demultiplexer_2_out_27[17], demultiplexer_2_out_27[18], demultiplexer_2_out_27[19], demultiplexer_2_out_27[20], demultiplexer_2_out_27[21], demultiplexer_2_out_27[22], demultiplexer_2_out_27[23], demultiplexer_2_out_27[24], demultiplexer_2_out_27[25], demultiplexer_2_out_27[26], demultiplexer_2_out_27[27], demultiplexer_2_out_27[28], demultiplexer_2_out_27[29], demultiplexer_2_out_27[30], demultiplexer_2_out_27[31], demultiplexer_2_out_26[0], demultiplexer_2_out_26[1], demultiplexer_2_out_26[2], demultiplexer_2_out_26[3], demultiplexer_2_out_26[4], demultiplexer_2_out_26[5], demultiplexer_2_out_26[6], demultiplexer_2_out_26[7], demultiplexer_2_out_26[8], demultiplexer_2_out_26[9], demultiplexer_2_out_26[10], demultiplexer_2_out_26[11], demultiplexer_2_out_26[12], demultiplexer_2_out_26[13], demultiplexer_2_out_26[14], demultiplexer_2_out_26[15], demultiplexer_2_out_26[16], demultiplexer_2_out_26[17], demultiplexer_2_out_26[18], demultiplexer_2_out_26[19], demultiplexer_2_out_26[20], demultiplexer_2_out_26[21], demultiplexer_2_out_26[22], demultiplexer_2_out_26[23], demultiplexer_2_out_26[24], demultiplexer_2_out_26[25], demultiplexer_2_out_26[26], demultiplexer_2_out_26[27], demultiplexer_2_out_26[28], demultiplexer_2_out_26[29], demultiplexer_2_out_26[30], demultiplexer_2_out_26[31], demultiplexer_2_out_25[0], demultiplexer_2_out_25[1], demultiplexer_2_out_25[2], demultiplexer_2_out_25[3], demultiplexer_2_out_25[4], demultiplexer_2_out_25[5], demultiplexer_2_out_25[6], demultiplexer_2_out_25[7], demultiplexer_2_out_25[8], demultiplexer_2_out_25[9], demultiplexer_2_out_25[10], demultiplexer_2_out_25[11], demultiplexer_2_out_25[12], demultiplexer_2_out_25[13], demultiplexer_2_out_25[14], demultiplexer_2_out_25[15], demultiplexer_2_out_25[16], demultiplexer_2_out_25[17], demultiplexer_2_out_25[18], demultiplexer_2_out_25[19], demultiplexer_2_out_25[20], demultiplexer_2_out_25[21], demultiplexer_2_out_25[22], demultiplexer_2_out_25[23], demultiplexer_2_out_25[24], demultiplexer_2_out_25[25], demultiplexer_2_out_25[26], demultiplexer_2_out_25[27], demultiplexer_2_out_25[28], demultiplexer_2_out_25[29], demultiplexer_2_out_25[30], demultiplexer_2_out_25[31], demultiplexer_2_out_24[0], demultiplexer_2_out_24[1], demultiplexer_2_out_24[2], demultiplexer_2_out_24[3], demultiplexer_2_out_24[4], demultiplexer_2_out_24[5], demultiplexer_2_out_24[6], demultiplexer_2_out_24[7], demultiplexer_2_out_24[8], demultiplexer_2_out_24[9], demultiplexer_2_out_24[10], demultiplexer_2_out_24[11], demultiplexer_2_out_24[12], demultiplexer_2_out_24[13], demultiplexer_2_out_24[14], demultiplexer_2_out_24[15], demultiplexer_2_out_24[16], demultiplexer_2_out_24[17], demultiplexer_2_out_24[18], demultiplexer_2_out_24[19], demultiplexer_2_out_24[20], demultiplexer_2_out_24[21], demultiplexer_2_out_24[22], demultiplexer_2_out_24[23], demultiplexer_2_out_24[24], demultiplexer_2_out_24[25], demultiplexer_2_out_24[26], demultiplexer_2_out_24[27], demultiplexer_2_out_24[28], demultiplexer_2_out_24[29], demultiplexer_2_out_24[30], demultiplexer_2_out_24[31], demultiplexer_2_out_23[0], demultiplexer_2_out_23[1], demultiplexer_2_out_23[2], demultiplexer_2_out_23[3], demultiplexer_2_out_23[4], demultiplexer_2_out_23[5], demultiplexer_2_out_23[6], demultiplexer_2_out_23[7], demultiplexer_2_out_23[8], demultiplexer_2_out_23[9], demultiplexer_2_out_23[10], demultiplexer_2_out_23[11], demultiplexer_2_out_23[12], demultiplexer_2_out_23[13], demultiplexer_2_out_23[14], demultiplexer_2_out_23[15], demultiplexer_2_out_23[16], demultiplexer_2_out_23[17], demultiplexer_2_out_23[18], demultiplexer_2_out_23[19], demultiplexer_2_out_23[20], demultiplexer_2_out_23[21], demultiplexer_2_out_23[22], demultiplexer_2_out_23[23], demultiplexer_2_out_23[24], demultiplexer_2_out_23[25], demultiplexer_2_out_23[26], demultiplexer_2_out_23[27], demultiplexer_2_out_23[28], demultiplexer_2_out_23[29], demultiplexer_2_out_23[30], demultiplexer_2_out_23[31], demultiplexer_2_out_22[0], demultiplexer_2_out_22[1], demultiplexer_2_out_22[2], demultiplexer_2_out_22[3], demultiplexer_2_out_22[4], demultiplexer_2_out_22[5], demultiplexer_2_out_22[6], demultiplexer_2_out_22[7], demultiplexer_2_out_22[8], demultiplexer_2_out_22[9], demultiplexer_2_out_22[10], demultiplexer_2_out_22[11], demultiplexer_2_out_22[12], demultiplexer_2_out_22[13], demultiplexer_2_out_22[14], demultiplexer_2_out_22[15], demultiplexer_2_out_22[16], demultiplexer_2_out_22[17], demultiplexer_2_out_22[18], demultiplexer_2_out_22[19], demultiplexer_2_out_22[20], demultiplexer_2_out_22[21], demultiplexer_2_out_22[22], demultiplexer_2_out_22[23], demultiplexer_2_out_22[24], demultiplexer_2_out_22[25], demultiplexer_2_out_22[26], demultiplexer_2_out_22[27], demultiplexer_2_out_22[28], demultiplexer_2_out_22[29], demultiplexer_2_out_22[30], demultiplexer_2_out_22[31], demultiplexer_2_out_21[0], demultiplexer_2_out_21[1], demultiplexer_2_out_21[2], demultiplexer_2_out_21[3], demultiplexer_2_out_21[4], demultiplexer_2_out_21[5], demultiplexer_2_out_21[6], demultiplexer_2_out_21[7], demultiplexer_2_out_21[8], demultiplexer_2_out_21[9], demultiplexer_2_out_21[10], demultiplexer_2_out_21[11], demultiplexer_2_out_21[12], demultiplexer_2_out_21[13], demultiplexer_2_out_21[14], demultiplexer_2_out_21[15], demultiplexer_2_out_21[16], demultiplexer_2_out_21[17], demultiplexer_2_out_21[18], demultiplexer_2_out_21[19], demultiplexer_2_out_21[20], demultiplexer_2_out_21[21], demultiplexer_2_out_21[22], demultiplexer_2_out_21[23], demultiplexer_2_out_21[24], demultiplexer_2_out_21[25], demultiplexer_2_out_21[26], demultiplexer_2_out_21[27], demultiplexer_2_out_21[28], demultiplexer_2_out_21[29], demultiplexer_2_out_21[30], demultiplexer_2_out_21[31], comparator_1_gt, comparator_1_lt, comparator_2_eq, comparator_2_lt, comparator_3_gt, comparator_3_eq, _12b[6], _12b[7], _12b[8], _12b[9], _12b[10], _12b[11], _12b[12], _12b[13], _12b[14], _12b[15], _12b[16], _12b[17], _12b[18], _12b[19], _12b[20], _12b[21], _12b[22], _12b[23], _12b[24], _12b[25], _12b[26], _12b[27], _12b[28], _12b[29], _12b[30], _12b[31], _16b[6], _16b[7], _16b[8], _16b[9], _16b[10], _16b[11], _16b[12], _16b[13], _16b[14], _16b[15], _16b[16], _16b[17], _16b[18], _16b[19], _16b[20], _16b[21], _16b[22], _16b[23], _16b[24], _16b[25], _16b[26], _16b[27], _16b[28], _16b[29], _16b[30], _16b[31], _19a[0], _19a[1], _19a[2], _19a[3], _19a[4], _19a[5], _19a[6], _19a[7], _19a[8], _19a[9], _19a[10], _19a[11], _19a[12], _19a[13], _19a[14], _19a[15], _19a[16], _19a[17], _19a[18], _19a[19], _19a[20], _19a[21], _19a[22], _19a[23], _19a[24], _19a[25], _19a[26], _19a[27], _19a[28], _19a[29], _19a[30], _19a[31], _19b[0], _19b[1], _19b[2], _19b[3], _19b[4], _19b[5], _19b[6], _19b[7], _19b[8], _19b[9], _19b[10], _19b[11], _19b[12], _19b[13], _19b[14], _19b[15], _19b[16], _19b[17], _19b[18], _19b[19], _19b[20], _19b[21], _19b[22], _19b[23], _19b[24], _19b[25], _19b[26], _19b[27], _19b[28], _19b[29], _19b[30], _19b[31], _20b[6], _20b[7], _20b[8], _20b[9], _20b[10], _20b[11], _20b[12], _20b[13], _20b[14], _20b[15], _20b[16], _20b[17], _20b[18], _20b[19], _20b[20], _20b[21], _20b[22], _20b[23], _20b[24], _20b[25], _20b[26], _20b[27], _20b[28], _20b[29], _20b[30], _20b[31]}

  // Other names for the same wires on the sheet: _12b_shifted[5:0] = _12b[5:0]; _20b_shifted[5:0] = _20b[5:0];
  //   OP[4:0] = OPCODE

  // Notes on the sheet:
  //   OPCODE: OPCODES:
  //   0: AND
  //   1: NAND
  //   2: OR
  //   3: NOR
  //   4: XOR
  //   5: XNOR
  //   6: NOT
  //   7: ADD
  //   8: SUB
  //   9: MUL
  //   10: DIV
  //   11: SHIFT (A shifted by B) left
  //   12: is A == to B
  //   13: NEGITIVE
  //   14: BIT COUNT
  //   15: Bit selector
  //   16: >
  //   17: <
  //   18: NOP: No Operation
  //   19: shift right
  //   20: PRNG, only A is used, A is the seed
  //   Inputs:
  //   A: input 1
  //   B: input 2
  //   Outputs: 
  //   Over: Overflow/remainder
  //   O: output from operation
endmodule
