// Digital circuit Hypertron 32bit ALU v1.0.dig as structural Verilog
module Hypertron_32bit_ALU_v1_0 (
  input  [3:0] OPCODE,
  input  [31:0] A,
  input  [31:0] B,
  output [31:0] O,
  output [31:0] Over
);

  wire add_1_c_o, bitselector_1_out, comparator_1_eq, comparator_1_gt, comparator_1_lt, sub_1_c_o;
  wire [5:0] bitcount_1_out;
  wire [31:0] _1a, _1b, _2a, _2b, _3a, _3b, _4a, _4b, _5a, _5b, _6a, _6b, _7a, _8a, _8b, _9a, _9b, _10a,
       _10b, _11a, _11b, _12a, _12b, _13a, _13b, _14a, _15a, _16a, _16b, demultiplexer_2_out_6,
       demultiplexer_2_out_13, demultiplexer_2_out_14, Out1, Out2, Out3, Out4, Out5, Out6, Out7, Out8, Out9,
       Out10, Out11, Out12, Out13, Out14, Out15, Out16, R1, R2, R3, R4;
  wire [63:0] bitextender_1_out;

  Demultiplexer #(.Bits(32), .Selector_Bits(4)) demultiplexer_1 (
    .sel(OPCODE), .in(A), .out_0(_1a), .out_1(_2a), .out_2(_3a), .out_3(_4a), .out_4(_5a), .out_5(_6a),
    .out_6(_7a), .out_7(_8a), .out_8(_9a), .out_9(_10a), .out_10(_11a), .out_11(_12a), .out_12(_13a),
    .out_13(_14a), .out_14(_15a), .out_15(_16a));
  Demultiplexer #(.Selector_Bits(4), .Bits(32)) demultiplexer_2 (
    .sel(OPCODE), .in(B), .out_0(_1b), .out_1(_2b), .out_2(_3b), .out_3(_4b), .out_4(_5b), .out_5(_6b),
    .out_6(demultiplexer_2_out_6), .out_7(_8b), .out_8(_9b), .out_9(_10b), .out_10(_11b), .out_11(_12b),
    .out_12(_13b), .out_13(demultiplexer_2_out_13), .out_14(demultiplexer_2_out_14), .out_15(_16b));
  BitExtender #(.inputBits(32), .outputBits(64)) bitextender_1 (.in(_16a), .out(bitextender_1_out));
  assign Out1 = _1a & _1b;  // And and_1, 32 bits wide
  assign Out2 = ~(_2a & _2b);  // NAnd nand_1, 32 bits wide
  assign Out3 = _3a | _3b;  // Or or_1, 32 bits wide
  assign Out4 = ~(_4a | _4b);  // NOr nor_1, 32 bits wide
  assign Out5 = _5a ^ _5b;  // XOr xor_1, 32 bits wide
  assign Out6 = ~(_6a ^ _6b);  // XNOr xnor_1, 32 bits wide
  assign Out7 = ~_7a;  // Not not_1, 32 bits wide
  Add #(.Bits(32)) add_1 (.a(_8a), .b(_8b), .c_i(1'b0), .s(Out8), .c_o(add_1_c_o));
  Sub #(.Bits(32)) sub_1 (.a(_9a), .b(_9b), .c_i(1'b0), .s(Out9), .c_o(sub_1_c_o));
  Mul #(.Bits(32)) mul_1 (.a(_10a), .b(_10b), .mul({R3, Out10}));
  Div #(.Bits(32)) div_1 (.a(_11a), .b(_11b), .q(Out11), .r(R4));
  BarrelShifter #(.Bits(32), .barrelShifterMode("arithmetic")) barrelshifter_1 (
    .in(_12a), .shift(_12b[5:0]), .out(Out12));
  Comparator #(.Bits(32)) comparator_1 (
    .a(_13a), .b(_13b), .gt(comparator_1_gt), .eq(comparator_1_eq), .lt(comparator_1_lt));
  Neg #(.Bits(32)) neg_1 (.in(_14a), .out(Out14));
  BitCount #(.Bits(32)) bitcount_1 (.in(_15a), .out(bitcount_1_out));
  BitSelector #(.Selector_Bits(6)) bitselector_1 (.in(bitextender_1_out), .sel(_16b[5:0]), .out(bitselector_1_out));
  BitExtender #(.inputBits(1), .outputBits(32)) bitextender_2 (.in(add_1_c_o), .out(R1));
  BitExtender #(.inputBits(1), .outputBits(32)) bitextender_3 (.in(sub_1_c_o), .out(R2));
  BitExtender #(.inputBits(1), .outputBits(32)) bitextender_4 (.in(comparator_1_eq), .out(Out13));
  BitExtender #(.inputBits(6), .outputBits(32)) bitextender_5 (.in(bitcount_1_out), .out(Out15));
  BitExtender #(.inputBits(1), .outputBits(32)) bitextender_6 (.in(bitselector_1_out), .out(Out16));
  Multiplexer #(.Bits(32), .Selector_Bits(4)) multiplexer_1 (
    .sel(OPCODE), .in_0(Out1), .in_1(Out2), .in_2(Out3), .in_3(Out4), .in_4(Out5), .in_5(Out6), .in_6(Out7),
    .in_7(Out8), .in_8(Out9), .in_9(Out10), .in_10(Out11), .in_11(Out12), .in_12(Out13), .in_13(Out14),
    .in_14(Out15), .in_15(Out16), .out(O));
  Multiplexer #(.Selector_Bits(4), .Bits(32)) multiplexer_2 (
    .sel(OPCODE), .in_0({32{1'b0}}), .in_1({32{1'b0}}), .in_2({32{1'b0}}), .in_3({32{1'b0}}),
    .in_4({32{1'b0}}), .in_5({32{1'b0}}), .in_6({32{1'b0}}), .in_7(R1), .in_8(R2), .in_9(R3), .in_10(R4),
    .in_11({32{1'b0}}), .in_12({32{1'b0}}), .in_13({32{1'b0}}), .in_14({32{1'b0}}), .in_15({32{1'b0}}),
    .out(Over));
  // also tied to GND on the sheet: {demultiplexer_2_out_6[0], demultiplexer_2_out_6[1], demultiplexer_2_out_6[2], demultiplexer_2_out_6[3], demultiplexer_2_out_6[4], demultiplexer_2_out_6[5], demultiplexer_2_out_6[6], demultiplexer_2_out_6[7], demultiplexer_2_out_6[8], demultiplexer_2_out_6[9], demultiplexer_2_out_6[10], demultiplexer_2_out_6[11], demultiplexer_2_out_6[12], demultiplexer_2_out_6[13], demultiplexer_2_out_6[14], demultiplexer_2_out_6[15], demultiplexer_2_out_6[16], demultiplexer_2_out_6[17], demultiplexer_2_out_6[18], demultiplexer_2_out_6[19], demultiplexer_2_out_6[20], demultiplexer_2_out_6[21], demultiplexer_2_out_6[22], demultiplexer_2_out_6[23], demultiplexer_2_out_6[24], demultiplexer_2_out_6[25], demultiplexer_2_out_6[26], demultiplexer_2_out_6[27], demultiplexer_2_out_6[28], demultiplexer_2_out_6[29], demultiplexer_2_out_6[30], demultiplexer_2_out_6[31], demultiplexer_2_out_13[0], demultiplexer_2_out_13[1], demultiplexer_2_out_13[2], demultiplexer_2_out_13[3], demultiplexer_2_out_13[4], demultiplexer_2_out_13[5], demultiplexer_2_out_13[6], demultiplexer_2_out_13[7], demultiplexer_2_out_13[8], demultiplexer_2_out_13[9], demultiplexer_2_out_13[10], demultiplexer_2_out_13[11], demultiplexer_2_out_13[12], demultiplexer_2_out_13[13], demultiplexer_2_out_13[14], demultiplexer_2_out_13[15], demultiplexer_2_out_13[16], demultiplexer_2_out_13[17], demultiplexer_2_out_13[18], demultiplexer_2_out_13[19], demultiplexer_2_out_13[20], demultiplexer_2_out_13[21], demultiplexer_2_out_13[22], demultiplexer_2_out_13[23], demultiplexer_2_out_13[24], demultiplexer_2_out_13[25], demultiplexer_2_out_13[26], demultiplexer_2_out_13[27], demultiplexer_2_out_13[28], demultiplexer_2_out_13[29], demultiplexer_2_out_13[30], demultiplexer_2_out_13[31], demultiplexer_2_out_14[0], demultiplexer_2_out_14[1], demultiplexer_2_out_14[2], demultiplexer_2_out_14[3], demultiplexer_2_out_14[4], demultiplexer_2_out_14[5], demultiplexer_2_out_14[6], demultiplexer_2_out_14[7], demultiplexer_2_out_14[8], demultiplexer_2_out_14[9], demultiplexer_2_out_14[10], demultiplexer_2_out_14[11], demultiplexer_2_out_14[12], demultiplexer_2_out_14[13], demultiplexer_2_out_14[14], demultiplexer_2_out_14[15], demultiplexer_2_out_14[16], demultiplexer_2_out_14[17], demultiplexer_2_out_14[18], demultiplexer_2_out_14[19], demultiplexer_2_out_14[20], demultiplexer_2_out_14[21], demultiplexer_2_out_14[22], demultiplexer_2_out_14[23], demultiplexer_2_out_14[24], demultiplexer_2_out_14[25], demultiplexer_2_out_14[26], demultiplexer_2_out_14[27], demultiplexer_2_out_14[28], demultiplexer_2_out_14[29], demultiplexer_2_out_14[30], demultiplexer_2_out_14[31], comparator_1_gt, comparator_1_lt, _12b[6], _12b[7], _12b[8], _12b[9], _12b[10], _12b[11], _12b[12], _12b[13], _12b[14], _12b[15], _12b[16], _12b[17], _12b[18], _12b[19], _12b[20], _12b[21], _12b[22], _12b[23], _12b[24], _12b[25], _12b[26], _12b[27], _12b[28], _12b[29], _12b[30], _12b[31], _16b[6], _16b[7], _16b[8], _16b[9], _16b[10], _16b[11], _16b[12], _16b[13], _16b[14], _16b[15], _16b[16], _16b[17], _16b[18], _16b[19], _16b[20], _16b[21], _16b[22], _16b[23], _16b[24], _16b[25], _16b[26], _16b[27], _16b[28], _16b[29], _16b[30], _16b[31]}

  // Other names for the same wires on the sheet: _12b_shifted[5:0] = _12b[5:0]; OP[3:0] = OPCODE

  // Notes on the sheet:
  //   OPCODE: OPCODES:
  //   1: AND
  //   2: NAND
  //   3: OR
  //   4: NOR
  //   5: XOR
  //   6: XNOR
  //   7: NOT
  //   8: ADD
  //   9: SUB
  //   10: MUL
  //   11: DIV
  //   12: SHIFT (A shifted by B)
  //   13: is A == to B
  //   14: NEGITIVE
  //   15: BIT COUNT
  //   16: Bit selector
  //   Inputs:
  //   A: input 1
  //   B: input 2
  //   Outputs: 
  //   Over: Overflow/remainder
  //   O: output from operation
endmodule
